// Logisim project HWproject (updated).circ as structural Verilog
module _1 (
  input  c_in,
  input  a,
  input  b,
  output sum,
  output c_out
);

  wire and_1_out, and_2_out, and_3_out, and_4_out, xor_1_out;

  and and_1 (and_1_out, a, b, c_in);
  ExactlyOne xor_1 (.out(xor_1_out), .in0(c_in), .in1(a), .in4(b));
  and and_2 (and_2_out, b, c_in);
  and and_3 (and_3_out, a, c_in);
  and and_4 (and_4_out, a, b);
  xor xor_2 (sum, and_1_out, xor_1_out);
  or or_1 (c_out, and_2_out, and_3_out, and_4_out);
endmodule

module _16 (
  input  in_1,
  input  [15:0] a,
  input  [15:0] b,
  input  c_out,
  output [15:0] sum
);

  wire n4_1_c_out, n4_2_c_out, n4_3_c_out;

  _4 u_4_1 (.c_in(in_1), .a(a[3:0]), .b(b[3:0]), .sum(sum[3:0]), .c_out(n4_1_c_out));
  _4 u_4_2 (.c_in(n4_1_c_out), .a(a[7:4]), .b(b[7:4]), .sum(sum[7:4]), .c_out(n4_2_c_out));
  _4 u_4_3 (.c_in(n4_2_c_out), .a(a[11:8]), .b(b[11:8]), .sum(sum[11:8]), .c_out(n4_3_c_out));
  _4 u_4_4 (.c_in(n4_3_c_out), .a(a[15:12]), .b(b[15:12]), .sum(sum[15:12]), .c_out(c_out));
endmodule

module _2__4 (
  input  c_in,
  input  [3:0] a,
  input  [3:0] b,
  output [3:0] sum,
  output c_out
);

  wire n1_1_c_out, n1_2_c_out, n1_3_c_out;

  _1 u_1_1 (.c_in(c_in), .a(a[0]), .b(b[0]), .sum(sum[0]), .c_out(n1_1_c_out));
  _1 u_1_2 (.c_in(n1_1_c_out), .a(a[1]), .b(b[1]), .sum(sum[1]), .c_out(n1_2_c_out));
  _1 u_1_3 (.c_in(n1_2_c_out), .a(a[2]), .b(b[2]), .sum(sum[2]), .c_out(n1_3_c_out));
  _1 u_1_4 (.c_in(n1_3_c_out), .a(a[3]), .b(b[3]), .sum(sum[3]), .c_out(c_out));
endmodule

module _4 (
  input  c_in,
  input  [3:0] a,
  input  [3:0] b,
  output [3:0] sum,
  output c_out
);

  _2__4 u_2_4_1 (.c_in(c_in), .a(a), .b(b), .sum(sum), .c_out(c_out));
endmodule

module _32 (
  input  in_1,
  input  [31:0] in_2,
  input  [31:0] in_3,
  input  c_out,
  output [31:0] out_5
);

  wire [15:0] n16_32_1_p6;

  // _16____32 16_32_1: pin names not known; wires that end beside it: in_1, in_1, in_2[15:0], in_3[15:0], out_5[15:0], n16_32_1_p6
  _16____32 u_16_32_2 (.in_1(n16_32_1_p6[0]), .a(n16_32_1_p6), .b(in_2[31:16]), .out_4(out_5[31:16]));
  // Pins of 1 and 16 bits meet at n16_32_1_p6
endmodule

module _16____32 (
  input  in_1,
  input  [15:0] a,
  input  [15:0] b,
  output [15:0] out_4
);

  _16 u_16_1 (.in_1(in_1), .a(a), .b(b), .sum(out_4));  // open: c_out
endmodule

module EXE (
  input  C_in,
  input  A,
  input  B,
  input  [2:0] Opcode,
  output Output,
  output Less,
  output C_out
);

  wire adder_1_out, and_1_out, or_1_out, subtractor_1_out;

  Adder #(.width(1)) adder_1 (.a(A), .b(B), .out(adder_1_out), .cin(C_in), .cout(C_out));
  and and_1 (and_1_out, A, B);
  or or_1 (or_1_out, A, B);
  Subtractor #(.width(1)) subtractor_1 (.a(A), .b(B), .out(subtractor_1_out), .bin(C_in), .bout(Less));
  Multiplexer #(.select(3)) multiplexer_1 (
    .in0(and_1_out), .in1(or_1_out), .in2(adder_1_out), .in3(subtractor_1_out), .out(Output), .sel(Opcode));  // open: in4, in5, in6, in7, en
endmodule

module ALU (
  input  [31:0] A,
  input  [31:0] B,
  input  [2:0] Opcode,
  input  C_in,
  output [31:0] out_5
);

  wire exe_1_c_out, exe_2_c_out, exe_3_c_out, exe_4_c_out, exe_5_c_out, exe_6_c_out, exe_7_c_out,
       exe_8_c_out, exe_9_c_out, exe_10_c_out, exe_11_c_out, exe_12_c_out, exe_13_c_out, exe_14_c_out,
       exe_15_c_out, exe_16_c_out, exe_17_c_out, exe_18_c_out, exe_19_c_out, exe_20_c_out, exe_21_c_out,
       exe_22_c_out, exe_23_c_out, exe_24_c_out, exe_25_c_out, exe_26_c_out, exe_27_c_out, exe_28_c_out,
       exe_29_c_out, exe_30_c_out, exe_31_c_out;

  // Probe on A
  // Probe on B
  EXE exe_1 (.C_in(C_in), .A(A[0]), .B(B[0]), .Opcode(Opcode), .Output(out_5[0]), .C_out(exe_1_c_out));  // open: Less
  EXE exe_2 (
    .C_in(exe_1_c_out), .A(A[1]), .B(B[1]), .Opcode(Opcode), .Output(out_5[1]), .C_out(exe_2_c_out));  // open: Less
  EXE exe_3 (
    .C_in(exe_2_c_out), .A(A[2]), .B(B[2]), .Opcode(Opcode), .Output(out_5[2]), .C_out(exe_3_c_out));  // open: Less
  EXE exe_4 (
    .C_in(exe_3_c_out), .A(A[3]), .B(B[3]), .Opcode(Opcode), .Output(out_5[3]), .C_out(exe_4_c_out));  // open: Less
  EXE exe_5 (
    .C_in(exe_4_c_out), .A(A[4]), .B(B[4]), .Opcode(Opcode), .Output(out_5[4]), .C_out(exe_5_c_out));  // open: Less
  EXE exe_6 (
    .C_in(exe_5_c_out), .A(A[5]), .B(B[5]), .Opcode(Opcode), .Output(out_5[5]), .C_out(exe_6_c_out));  // open: Less
  EXE exe_7 (
    .C_in(exe_6_c_out), .A(A[6]), .B(B[6]), .Opcode(Opcode), .Output(out_5[6]), .C_out(exe_7_c_out));  // open: Less
  EXE exe_8 (
    .C_in(exe_7_c_out), .A(A[7]), .B(B[7]), .Opcode(Opcode), .Output(out_5[7]), .C_out(exe_8_c_out));  // open: Less
  EXE exe_9 (
    .C_in(exe_8_c_out), .A(A[8]), .B(B[8]), .Opcode(Opcode), .Output(out_5[8]), .C_out(exe_9_c_out));  // open: Less
  EXE exe_10 (
    .C_in(exe_9_c_out), .A(A[9]), .B(B[9]), .Opcode(Opcode), .Output(out_5[9]), .C_out(exe_10_c_out));  // open: Less
  EXE exe_11 (
    .C_in(exe_10_c_out), .A(A[10]), .B(B[10]), .Opcode(Opcode), .Output(out_5[10]), .C_out(exe_11_c_out));  // open: Less
  EXE exe_12 (
    .C_in(exe_11_c_out), .A(A[11]), .B(B[11]), .Opcode(Opcode), .Output(out_5[11]), .C_out(exe_12_c_out));  // open: Less
  EXE exe_13 (
    .C_in(exe_12_c_out), .A(A[12]), .B(B[12]), .Opcode(Opcode), .Output(out_5[12]), .C_out(exe_13_c_out));  // open: Less
  EXE exe_14 (
    .C_in(exe_13_c_out), .A(A[13]), .B(B[13]), .Opcode(Opcode), .Output(out_5[13]), .C_out(exe_14_c_out));  // open: Less
  EXE exe_15 (
    .C_in(exe_14_c_out), .A(A[14]), .B(B[14]), .Opcode(Opcode), .Output(out_5[14]), .C_out(exe_15_c_out));  // open: Less
  EXE exe_16 (
    .C_in(exe_15_c_out), .A(A[15]), .B(B[15]), .Opcode(Opcode), .Output(out_5[15]), .C_out(exe_16_c_out));  // open: Less
  EXE exe_17 (
    .C_in(exe_16_c_out), .A(A[16]), .B(B[16]), .Opcode(Opcode), .Output(out_5[16]), .C_out(exe_17_c_out));  // open: Less
  EXE exe_18 (
    .C_in(exe_17_c_out), .A(A[17]), .B(B[17]), .Opcode(Opcode), .Output(out_5[17]), .C_out(exe_18_c_out));  // open: Less
  EXE exe_19 (
    .C_in(exe_18_c_out), .A(A[18]), .B(B[18]), .Opcode(Opcode), .Output(out_5[18]), .C_out(exe_19_c_out));  // open: Less
  EXE exe_20 (
    .C_in(exe_19_c_out), .A(A[19]), .B(B[19]), .Opcode(Opcode), .Output(out_5[19]), .C_out(exe_20_c_out));  // open: Less
  EXE exe_21 (
    .C_in(exe_20_c_out), .A(A[20]), .B(B[20]), .Opcode(Opcode), .Output(out_5[20]), .C_out(exe_21_c_out));  // open: Less
  EXE exe_22 (
    .C_in(exe_21_c_out), .A(A[21]), .B(B[21]), .Opcode(Opcode), .Output(out_5[21]), .C_out(exe_22_c_out));  // open: Less
  EXE exe_23 (
    .C_in(exe_22_c_out), .A(A[22]), .B(B[22]), .Opcode(Opcode), .Output(out_5[22]), .C_out(exe_23_c_out));  // open: Less
  EXE exe_24 (
    .C_in(exe_23_c_out), .A(A[23]), .B(B[23]), .Opcode(Opcode), .Output(out_5[23]), .C_out(exe_24_c_out));  // open: Less
  EXE exe_25 (
    .C_in(exe_24_c_out), .A(A[24]), .B(B[24]), .Opcode(Opcode), .Output(out_5[24]), .C_out(exe_25_c_out));  // open: Less
  EXE exe_26 (
    .C_in(exe_25_c_out), .A(A[25]), .B(B[25]), .Opcode(Opcode), .Output(out_5[25]), .C_out(exe_26_c_out));  // open: Less
  EXE exe_27 (
    .C_in(exe_26_c_out), .A(A[26]), .B(B[26]), .Opcode(Opcode), .Output(out_5[26]), .C_out(exe_27_c_out));  // open: Less
  EXE exe_28 (
    .C_in(exe_27_c_out), .A(A[27]), .B(B[27]), .Opcode(Opcode), .Output(out_5[27]), .C_out(exe_28_c_out));  // open: Less
  EXE exe_29 (
    .C_in(exe_28_c_out), .A(A[28]), .B(B[28]), .Opcode(Opcode), .Output(out_5[28]), .C_out(exe_29_c_out));  // open: Less
  EXE exe_30 (
    .C_in(exe_29_c_out), .A(A[29]), .B(B[29]), .Opcode(Opcode), .Output(out_5[29]), .C_out(exe_30_c_out));  // open: Less
  EXE exe_31 (
    .C_in(exe_30_c_out), .A(A[30]), .B(B[30]), .Opcode(Opcode), .Output(out_5[30]), .C_out(exe_31_c_out));  // open: Less
  EXE exe_32 (.C_in(exe_31_c_out), .A(A[31]), .B(B[31]), .Opcode(Opcode), .Output(out_5[31]));  // open: Less, C_out
  // Probe on out_5
endmodule
