// Logisim project HWproject.circ as structural Verilog
module _1 (
  input  c_in,
  input  a,
  input  b,
  output sum,
  output c_out
);

  wire and_1_out, and_2_out, and_3_out, and_4_out, xor_1_out;

  and and_1 (and_1_out, a, b, c_in);
  ExactlyOne xor_1 (.out(xor_1_out), .in0(c_in), .in1(a), .in4(b));
  and and_2 (and_2_out, b, c_in);
  and and_3 (and_3_out, a, c_in);
  and and_4 (and_4_out, a, b);
  xor xor_2 (sum, and_1_out, xor_1_out);
  or or_1 (c_out, and_2_out, and_3_out, and_4_out);
endmodule

module _32 (
  input  c_in,
  input  [31:0] a,
  input  [31:0] b
);

  wire n1_1_c_out, n1_1_sum, n1_2_c_out, n1_2_sum, n1_3_c_out, n1_3_sum, n1_4_c_out, n1_4_sum, n1_5_c_out,
       n1_5_sum, n1_6_c_out, n1_6_sum, n1_7_c_out, n1_7_sum, n1_8_c_out, n1_8_sum, n1_9_c_out, n1_9_sum,
       n1_10_c_out, undriven;

  _1 u_1_1 (.c_in(c_in), .a(a[0]), .b(b[0]), .sum(n1_1_sum), .c_out(n1_1_c_out));
  _1 u_1_2 (.c_in(n1_1_c_out), .a(a[1]), .b(undriven), .sum(n1_2_sum), .c_out(n1_2_c_out));
  _1 u_1_3 (.c_in(n1_2_c_out), .a(a[2]), .sum(n1_3_sum), .c_out(n1_3_c_out));  // open: b
  _1 u_1_4 (.c_in(n1_3_c_out), .a(a[3]), .sum(n1_4_sum), .c_out(n1_4_c_out));  // open: b
  _1 u_1_5 (.c_in(n1_4_c_out), .a(a[4]), .sum(n1_5_sum), .c_out(n1_5_c_out));  // open: b
  _1 u_1_6 (.c_in(n1_5_c_out), .a(a[5]), .sum(n1_6_sum), .c_out(n1_6_c_out));  // open: b
  _1 u_1_7 (.c_in(n1_6_c_out), .a(a[6]), .sum(n1_7_sum), .c_out(n1_7_c_out));  // open: b
  _1 u_1_8 (.c_in(n1_7_c_out), .a(a[7]), .sum(n1_8_sum), .c_out(n1_8_c_out));  // open: b
  _1 u_1_9 (.c_in(n1_8_c_out), .a(a[8]), .sum(n1_9_sum), .c_out(n1_9_c_out));  // open: b
  _1 u_1_10 (.c_in(n1_9_c_out), .c_out(n1_10_c_out));  // open: a, b, sum
  _1 u_1_11 (.c_in(n1_10_c_out));  // open: a, b, sum, c_out
  _1 u_1_12 ();  // open: c_in, a, b, sum, c_out
  _1 u_1_13 ();  // open: c_in, a, b, sum, c_out
  _1 u_1_14 ();  // open: c_in, a, b, sum, c_out
endmodule

module _8 (
  input  in_1,
  input  [15:0] a,
  input  [15:0] sum,
  input  [15:0] b,
  input  c_out
);

  wire n4_1_c_out, n4_2_c_out, n4_3_c_out;

  _4 u_4_1 (.c_in(in_1), .a(a[3:0]), .b(b[3:0]), .sum(sum[3:0]), .c_out(n4_1_c_out));
  _4 u_4_2 (.c_in(n4_1_c_out), .a(a[7:4]), .b(b[7:4]), .sum(sum[7:4]), .c_out(n4_2_c_out));
  _4 u_4_3 (.c_in(n4_2_c_out), .a(a[11:8]), .b(b[11:8]), .sum(sum[11:8]), .c_out(n4_3_c_out));
  _4 u_4_4 (.c_in(n4_3_c_out), .a(a[15:12]), .b(b[15:12]), .sum(sum[15:12]), .c_out(c_out));
endmodule

module _2__4 (
  input  c_in,
  input  [3:0] a,
  input  [3:0] b,
  output [3:0] sum,
  output c_out
);

  wire n1_1_c_out, n1_2_c_out, n1_3_c_out;

  _1 u_1_1 (.c_in(c_in), .a(a[0]), .b(b[0]), .sum(sum[0]), .c_out(n1_1_c_out));
  _1 u_1_2 (.c_in(n1_1_c_out), .a(a[1]), .b(b[1]), .sum(sum[1]), .c_out(n1_2_c_out));
  _1 u_1_3 (.c_in(n1_2_c_out), .a(a[2]), .b(b[2]), .sum(sum[2]), .c_out(n1_3_c_out));
  _1 u_1_4 (.c_in(n1_3_c_out), .a(a[3]), .b(b[3]), .sum(sum[3]), .c_out(c_out));
endmodule

module _4 (
  input  c_in,
  input  [3:0] a,
  input  [3:0] b,
  output [3:0] sum,
  output c_out
);

  _2__4 u_2_4_1 (.c_in(c_in), .a(a), .b(b), .sum(sum), .c_out(c_out));
endmodule

module _2test (
  input  c_in,
  input  [3:0] a,
  input  [3:0] b,
  output [3:0] sum,
  output c_out
);

  wire n1test_1_c_out, n1test_2_c_out, n1test_3_c_out;

  _1test u_1test_1 (.c_in(c_in), .a(a[0]), .b(b[0]), .sum(sum[0]), .c_out(n1test_1_c_out));
  _1test u_1test_2 (.c_in(n1test_1_c_out), .a(a[1]), .b(b[1]), .sum(sum[1]), .c_out(n1test_2_c_out));
  _1test u_1test_3 (.c_in(n1test_2_c_out), .a(a[2]), .b(b[2]), .sum(sum[2]), .c_out(n1test_3_c_out));
  _1test u_1test_4 (.c_in(n1test_3_c_out), .a(a[3]), .b(b[3]), .sum(sum[3]), .c_out(c_out));
endmodule

module _1test (
  input  c_in,
  input  a,
  input  b,
  output sum,
  output c_out
);

  wire and_1_out, and_2_out, xor_1_out;

  xor xor_1 (xor_1_out, a, b);
  and and_1 (and_1_out, c_in, xor_1_out);
  and and_2 (and_2_out, a, b);
  xor xor_2 (sum, xor_1_out, c_in);
  or or_1 (c_out, and_1_out, and_2_out);
endmodule

module _8test (
  input  in_1,
  input  [15:0] a,
  input  [15:0] sum,
  input  [15:0] b,
  input  c_out
);

  wire n2test_1_c_out, n2test_2_c_out, n2test_3_c_out;

  _2test u_2test_1 (.c_in(in_1), .a(a[3:0]), .b(b[3:0]), .sum(sum[3:0]), .c_out(n2test_1_c_out));
  _2test u_2test_2 (.c_in(n2test_1_c_out), .a(a[7:4]), .b(b[7:4]), .sum(sum[7:4]), .c_out(n2test_2_c_out));
  _2test u_2test_3 (.c_in(n2test_2_c_out), .a(a[11:8]), .b(b[11:8]), .sum(sum[11:8]), .c_out(n2test_3_c_out));
  _2test u_2test_4 (.c_in(n2test_3_c_out), .a(a[15:12]), .b(b[15:12]), .sum(sum[15:12]), .c_out(c_out));
endmodule
